// Logisim project hw1.circ as structural Verilog: 1 circuit, main circuit main
module main (
);

  wire and_1_out, and_2_out, and_3_out, and_5_out, and_10_out, and_13_out, and_14_out, and_15_out,
       and_16_out, nor_1_out, nor_2_out, nor_4_out, nor_6_out, not_1_out, not_2_out, not_4_out, not_5_out,
       not_6_out, not_7_out, not_9_out, not_11_out, undriven, undriven_2;
  wire [1:0] and_4_out, and_6_out, and_7_out, and_8_out, and_9_out, bit_extender_1_out, bit_extender_2_out,
       bit_extender_3_out, bit_extender_4_out, not_3_out, or_1_out, or_2_out, xnor_1_out, xnor_2_out;

  not not_1 (not_1_out, 1'b1);
  not not_2 (not_2_out, 1'b1);
  assign xnor_1_out = ~(2'b01 ^ 2'b01);  // XNOR_Gate xnor_1, 2 bits wide
  nor nor_1 (nor_1_out, 1'b1, 1'b1);
  and and_1 (and_1_out, not_1_out, 1'b1);
  and and_2 (and_2_out, 1'b1, not_2_out);
  and and_3 (and_3_out, 1'b1, 1'b1);
  assign and_4_out = 2'b01 & 2'b01;  // AND_Gate and_4, 2 bits wide
  assign not_3_out = ~2'b01;  // NOT_Gate not_3, 2 bits wide
  assign xnor_2_out = ~(2'b01 ^ 2'b01);  // XNOR_Gate xnor_2, 2 bits wide
  assign or_1_out = 2'b01 | 2'b01;  // OR_Gate or_1, 2 bits wide
  and and_5 (and_5_out, xnor_1_out[0], xnor_1_out[1]);
  assign bit_extender_1_out = {{1{nor_1_out}}, nor_1_out};  // Bit_Extender bit_extender_1
  assign bit_extender_2_out = {{1{and_1_out}}, and_1_out};  // Bit_Extender bit_extender_2
  assign bit_extender_3_out = {{1{and_2_out}}, and_2_out};  // Bit_Extender bit_extender_3
  assign bit_extender_4_out = {{1{and_3_out}}, and_3_out};  // Bit_Extender bit_extender_4
  assign and_6_out = xnor_2_out & bit_extender_1_out;  // AND_Gate and_6, 2 bits wide
  assign and_7_out = and_4_out & bit_extender_2_out;  // AND_Gate and_7, 2 bits wide
  assign and_8_out = or_1_out & bit_extender_3_out;  // AND_Gate and_8, 2 bits wide
  assign and_9_out = not_3_out & bit_extender_4_out;  // AND_Gate and_9, 2 bits wide
  assign or_2_out = and_6_out | and_7_out | and_8_out | and_9_out;  // OR_Gate or_2, 2 bits wide
  not not_4 (not_4_out, undriven_2);
  not not_5 (not_5_out, undriven_2);
  not not_6 (not_6_out, undriven_2);
  not not_7 (not_7_out, undriven);
  not not_8 (not_7_out, undriven);
  not not_9 (not_9_out, undriven);
  not not_10 (not_9_out, undriven);
  not not_11 (not_11_out, undriven);
  and and_10 (and_10_out, not_7_out, undriven_2);
  not not_12 (not_11_out, undriven);
  not not_13 (not_11_out, undriven);
  and and_11 (and_10_out, not_9_out, undriven_2);
  and and_12 (and_10_out, not_11_out, undriven_2);
  and and_13 (and_13_out, undriven, not_4_out);
  and and_14 (and_14_out, undriven, not_5_out);
  not not_14 (not_4_out, undriven_2);
  and and_15 (and_15_out, undriven, not_6_out);
  not not_15 (not_5_out, undriven_2);
  not not_16 (not_6_out, undriven_2);
  not not_17 (not_6_out, undriven_2);
  and and_16 (and_16_out, undriven, undriven_2);
  and and_17 (and_16_out, undriven, undriven_2);
  and and_18 (and_16_out, undriven, undriven_2);
  nor nor_2 (nor_2_out, undriven, undriven_2);
  nor nor_3 (nor_2_out, undriven, undriven_2);
  nor nor_4 (nor_4_out, undriven, undriven_2);
  nor nor_5 (nor_4_out, undriven, undriven_2);
  nor nor_6 (nor_6_out, undriven, undriven_2);
  nor nor_7 (nor_6_out, undriven, undriven_2);
  nor nor_8 (nor_6_out, undriven, undriven_2);
  and and_19 (and_10_out, not_7_out, undriven_2);
  and and_20 (and_10_out, not_9_out, undriven_2);
  and and_21 (and_10_out, not_11_out, undriven_2);
  and and_22 (and_10_out, not_11_out, undriven_2);
  and and_23 (and_13_out, undriven, not_4_out);
  and and_24 (and_14_out, undriven, not_5_out);
  and and_25 (and_15_out, undriven, not_6_out);
  and and_26 (and_15_out, undriven, not_6_out);
  and and_27 (and_16_out, undriven, undriven_2);
  and and_28 (and_16_out, undriven, undriven_2);
  and and_29 (and_16_out, undriven, undriven_2);
  and and_30 (and_16_out, undriven, undriven_2);

  // Notes on the sheet:
  //   A
  //   B
  //   A
  //   B
endmodule
